# Fritzing sketch Esquema_elétrico (saved by Fritzing 0.9.9b)
breadboards: 1

parts:
  Mod1 = Raspberry Pi Pico
  M1 = gear-motor
  M2 = gear-motor
  M3 = gear-motor
  M4 = gear-motor
  WATER_PUMP1 = water pump/motor
  VCC1 = Battery block 9V
  Componente1 = Bluetooth HC-05 Macho
  J1 = Basic Servo
  LLC1 = Logic Level Converter [package="Breakout board"]
  KF-1 = KF-301 Relay [package=THT]
  A2 = L298N DC motor driver
  A3 = L298N DC motor driver

nets:
  N1: Mod1.pin_1, Componente1.TXD
  N2: Mod1.pin_2, Componente1.RXD
  GND: Mod1.pin_3, Mod1.pin_8, Mod1.pin_13, Mod1.pin_18, Mod1.pin_23, Mod1.pin_28, Mod1.pin_33, Mod1.pin_38, Mod1.pin_42, WATER_PUMP1.pin_1, VCC1.-, Componente1.GND, J1.gnd, LLC1.L-GND, LLC1.H-GND, KF-1.ground, A2.GND, A3.GND
  N3: Mod1.pin_4, J1.pulse
  N4: Mod1.pin_14, A3.IN1
  N5: Mod1.pin_15, A3.IN2
  N6: Mod1.pin_16, A3.IN3
  N7: Mod1.pin_17, A3.IN4
  N8: Mod1.pin_21, LLC1.LV1
  N9: Mod1.pin_24, A2.IN4
  N10: Mod1.pin_25, A2.IN3
  N11: Mod1.pin_26, A2.IN2
  N12: Mod1.pin_27, A2.IN1
  N13: Mod1.pin_36, LLC1.LV
  VCC: Mod1.pin_40, Componente1.VCC, J1.vcc, A3.5V, A3.+5V-J1, A3.+5V-J2, A3.ENA, A3.ENB
  N14: M1.pin_1, A2.OUT4
  N15: M1.pin_2, A2.OUT3
  N16: M2.pin_1, A2.OUT2
  N17: M2.pin_2, A2.OUT1
  N18: M3.pin_1, A3.OUT4
  N19: M3.pin_2, A3.OUT3
  N20: M4.pin_1, A3.OUT2
  N21: M4.pin_2, A3.OUT1
  N22: WATER_PUMP1.pin_2, KF-1.NO
  12V: VCC1.+, A2.12V, A3.12V
  N23: LLC1.HV, KF-1.power, KF-1.C, A2.5V, A2.+5V-J1, A2.+5V-J2, A2.ENA, A2.ENB
  N24: LLC1.HV1, KF-1.signal

custom parts:
  Raspberry Pi Pico: Raspberry Pi Pico. Based around the RP2040 microcontroller the Pico is a low cost microcontroller device bringing Raspberry Pi quality, cost, and easy of use to the microcontroller space. Jan 2021, Split part in to two versions: SMD (this one) and tht. This one is single sided and uses the castellation pads to solder the module to the board (no holes, other than for the USB connector!). The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
  water pump/motor: WATER PUMP BY ARDUBLOCKTR
  Logic Level Converter: 5V to/from 3.3V logic level converter
  KF-301 Relay: KF-301
  L298N DC motor driver: This L298N Motor Driver Module is a high power motor driver module for driving DC and Stepper Motors. This module consists of an L298 motor driver IC and a 78M05 5V regulator.
